# Fritzing sketch 光敏追光器 (saved by Fritzing 0.9.3b)
circuit board: 8.47092cm x 8.98355cm
breadboards: 1

parts:
  R1 = Resistor [tolerance=±5% resistance=10 package=THT]
  R2 = Resistor [tolerance=±5% resistance=220 package=THT]
  IC1 = IC, DIP package, 8 pins [chip_label=IC]
  R3 = Photocell (LDR) [package=THT]
  R4 = Photocell (LDR) [package=THT]
  VCC1 = Battery
  M1 = DC Motor
  R5 = Resistor [tolerance=±5% resistance=10 package=THT]
  R6 = Resistor [tolerance=±5% resistance=220 package=THT]
  IC2 = IC, DIP package, 8 pins [chip_label=IC]
  R7 = Photocell (LDR) [package=THT]
  R8 = Photocell (LDR) [package=THT]
  VCC2 = Battery
  M2 = DC Motor
  R9 = Resistor [tolerance=±5% resistance=10 package=THT]
  R10 = Resistor [tolerance=±5% resistance=220 package=THT]
  IC3 = IC, DIP package, 8 pins [chip_label=IC]
  R11 = Photocell (LDR) [package=THT]
  R12 = Photocell (LDR) [package=THT]
  VCC3 = Battery
  M3 = DC Motor
  R13 = Resistor [tolerance=±5% resistance=10 package=THT]
  R14 = Resistor [tolerance=±5% resistance=220 package=THT]
  IC4 = IC, DIP package, 8 pins [chip_label=IC]
  R15 = Photocell (LDR) [package=THT]
  R16 = Photocell (LDR) [package=THT]
  VCC4 = Battery
  M4 = DC Motor
  R17 = Resistor [tolerance=±5% resistance=10 package=THT]
  R18 = Resistor [tolerance=±5% resistance=10 package=THT]
  R19 = Resistor [tolerance=±5% resistance=10 package=THT]
  R20 = Resistor [tolerance=±5% resistance=10 package=THT]
  R21 = Resistor [tolerance=±5% resistance=220 package=THT]
  R22 = Resistor [tolerance=±5% resistance=220 package=THT]
  R23 = Resistor [tolerance=±5% resistance=220 package=THT]
  R24 = Resistor [tolerance=±5% resistance=220 package=THT]
  IC5 = IC, DIP package, 8 pins [chip_label=IC]
  IC6 = IC, DIP package, 8 pins [chip_label=IC]
  IC7 = IC, DIP package, 8 pins [chip_label=IC]
  IC8 = IC, DIP package, 8 pins [chip_label=IC]
  R25 = Photocell (LDR) [package=THT]
  R26 = Photocell (LDR) [package=THT]
  R27 = Photocell (LDR) [package=THT]
  R28 = Photocell (LDR) [package=THT]
  R29 = Photocell (LDR) [package=THT]
  R30 = Photocell (LDR) [package=THT]
  R31 = Photocell (LDR) [package=THT]
  R32 = Photocell (LDR) [package=THT]
  VCC5 = Battery
  VCC6 = Battery
  VCC7 = Battery
  VCC8 = Battery
  M5 = DC Motor
  M6 = DC Motor
  M7 = DC Motor
  M8 = DC Motor

nets:
  N1: R1.Pin_0, IC1.pin2, R4.pin_0, VCC1.+
  N2: R1.Pin_1, R2.Pin_0, IC1.pin5, IC1.pin7
  N3: R2.Pin_1, IC1.pin4, R3.pin_0, VCC1.-
  N4: IC1.pin1, M1.pin_1
  N5: IC1.pin3, M1.pin_2
  N6: IC1.pin6, IC1.pin8, R3.pin_1, R4.pin_1
  N7: R5.Pin_0, IC2.pin2, R8.pin_0, VCC2.+
  N8: R5.Pin_1, R6.Pin_0, IC2.pin5, IC2.pin7
  N9: R6.Pin_1, IC2.pin4, R7.pin_0, VCC2.-
  N10: IC2.pin1, M2.pin_1
  N11: IC2.pin3, M2.pin_2
  N12: IC2.pin6, IC2.pin8, R7.pin_1, R8.pin_1
  N13: R9.Pin_0, IC3.pin2, R12.pin_0, VCC3.+
  N14: R9.Pin_1, R10.Pin_0, IC3.pin5, IC3.pin7
  N15: R10.Pin_1, IC3.pin4, R11.pin_0, VCC3.-
  N16: IC3.pin1, M3.pin_1
  N17: IC3.pin3, M3.pin_2
  N18: IC3.pin6, IC3.pin8, R11.pin_1, R12.pin_1
  N19: R13.Pin_0, IC4.pin2, R16.pin_0, VCC4.+
  N20: R13.Pin_1, R14.Pin_0, IC4.pin5, IC4.pin7
  N21: R14.Pin_1, IC4.pin4, R15.pin_0, VCC4.-
  N22: IC4.pin1, M4.pin_1
  N23: IC4.pin3, M4.pin_2
  N24: IC4.pin6, IC4.pin8, R15.pin_1, R16.pin_1
  N25: R17.Pin_0, IC6.pin2, R31.pin_0, VCC8.+
  N26: R17.Pin_1, R22.Pin_0, IC6.pin5, IC6.pin7
  N27: R18.Pin_0, IC7.pin2, R32.pin_0, VCC7.+
  N28: R18.Pin_1, R23.Pin_0, IC7.pin5, IC7.pin7
  N29: R19.Pin_0, IC8.pin2, R29.pin_0, VCC5.+
  N30: R19.Pin_1, R21.Pin_0, IC8.pin5, IC8.pin7
  N31: R20.Pin_0, IC5.pin2, R30.pin_0, VCC6.+
  N32: R20.Pin_1, R24.Pin_0, IC5.pin5, IC5.pin7
  N33: R21.Pin_1, IC8.pin4, R28.pin_0, VCC5.-
  N34: R22.Pin_1, IC6.pin4, R27.pin_0, VCC8.-
  N35: R23.Pin_1, IC7.pin4, R25.pin_0, VCC7.-
  N36: R24.Pin_1, IC5.pin4, R26.pin_0, VCC6.-
  N37: IC5.pin1, M7.pin_1
  N38: IC5.pin3, M7.pin_2
  N39: IC5.pin6, IC5.pin8, R26.pin_1, R30.pin_1
  N40: IC6.pin1, M8.pin_1
  N41: IC6.pin3, M8.pin_2
  N42: IC6.pin6, IC6.pin8, R27.pin_1, R31.pin_1
  N43: IC7.pin1, M6.pin_1
  N44: IC7.pin3, M6.pin_2
  N45: IC7.pin6, IC7.pin8, R25.pin_1, R32.pin_1
  N46: IC8.pin1, M5.pin_1
  N47: IC8.pin3, M5.pin_2
  N48: IC8.pin6, IC8.pin8, R28.pin_1, R29.pin_1
